# Fritzing sketch Schéma_des_connexions (saved by Fritzing 0.9.1b)
breadboards: 1

parts:
  Part1 = Arduino Uno (Rev3)
  DHT1 = DHT11 Humitidy and Temperature Sensor
  R1 = PHOTOCELL [package=photocell]
  R2 = Resistor [tolerance=±5% resistance=4.7k package=THT]
  R3 = Resistor [tolerance=±5% resistance=10k package=THT]
  RF1 = nRF8001 Bluetooth LE Breakout

nets:
  N1: Part1.A0, R1.P$1, R3.Pin_0
  N2: Part1.D8, R2.Pin_1
  N3: Part1.D9_PWM, RF1.RST
  N4: Part1.D10_PWM/SS, RF1.REQ
  N5: Part1.D11_PWM/MOSI, RF1.MOSI
  N6: Part1.D12/MISO, RF1.MISO
  N7: Part1.D13/SCK, RF1.SCK
  N8: Part1.D2, RF1.RDY
  5V: Part1.5V, DHT1.VDD, R1.P$2, RF1.VIN
  GND: Part1.VIN, DHT1.GND, R3.Pin_1, RF1.GND
  N9: DHT1.DATA, R2.Pin_0

custom parts:
  DHT11 Humitidy and Temperature Sensor: DHT11 Humidity and Temperature Sensor
  nRF8001 Bluetooth LE Breakout: nRF8001 Breakout Board
